# Fritzing sketch schematic (saved by Fritzing 1.0.6)
breadboards: 1

parts:
  M1 = STM32F103C8T6 blue mini board
  Mod1 = Raspberry Pi 4B
  U1 = LIPO-2000mAh [package=lipo-2000]
  M2 = RioRand LM2596
  M3 = RioRand LM2596
  Part1 = Motor Driver 1A Dual TB6612FNG
  Part2 = Motor Driver 1A Dual TB6612FNG
  Part3 = InvenSense MPU6050
  M5 = DC Motor [voltage_(max)=6V voltage_(min)=3V]
  M6 = DC Motor [voltage_(max)=6V voltage_(min)=3V]
  M7 = DC Motor [voltage_(max)=6V voltage_(min)=3V]
  M4 = DC Motor [voltage_(max)=6V voltage_(min)=3V]
  Yumo-enc1 = YumoE6B2
  Yumo-enc2 = YumoE6B2
  Yumo-enc3 = YumoE6B2
  Yumo-enc4 = YumoE6B2
  Part6 = CAN-Bus Shield
  Part7 = CAN-Bus Shield

nets:
  N1: M1.B12, Part2.AIN2
  N2: M1.B14, Part2.BIN2
  N3: M1.B15, Part2.BIN1
  N4: M1.A8, Part1.PWMA
  N5: M1.A9, Part1.PWMB
  N6: M1.A11, Part2.PWMB
  N7: M1.A15, Yumo-enc4.A
  N8: M1.B3, Yumo-enc4.B
  N9: M1.B4, Yumo-enc3.A
  N10: M1.B5, Part7.MOSI
  N11: M1.B6, Yumo-enc2.A
  N12: M1.B7, Yumo-enc2.B
  N13: M1.B8, Part7.CAN_INT
  N14: M1.B9, Part7.CAN_CS
  5V: M1.5V, M3.Pin_3, Part7.5V
  GND: M1.G, M1.GND, Mod1.GND, U1.-, M2.Pin_2, M2.Pin_4, M3.Pin_2, M3.Pin_4, Part1.GND, Part2.GND, Part3.GND, Yumo-enc1.GND, Yumo-enc2.GND, Yumo-enc3.GND, Yumo-enc4.GND, Part6.GND, Part7.GND
  VCC: M1.3.3V, Part1.VCC, Part1.STBY, Part2.VCC, Part2.STBY, Yumo-enc1.V, Yumo-enc2.V, Yumo-enc3.V, Yumo-enc4.V
  N15: M1.A0, Yumo-enc1.A
  N16: M1.A1, Yumo-enc1.B
  N17: M1.A5, Part7.SCK
  N18: M1.A6, Part7.MISO
  N19: M1.A7, Yumo-enc3.B
  N20: M1.B0, Part1.AIN2
  N21: M1.B11, Part1.BIN2
  5V_2: Mod1.5V, M2.Pin_3, Part6.5V
  N22: Mod1.GPIO2, Part3.SDA
  N23: Mod1.GPIO3, Part3.SCL
  3V3: Mod1.3V3, Part3.VCC, Part3.AD0
  N24: Mod1.GPIO24, Part3.INT
  N25: Mod1.GPIO10, Part6.MOSI
  N26: Mod1.GPIO9, Part6.MISO
  N27: Mod1.GPIO25, Part6.CAN_INT
  N28: Mod1.GPIO11, Part6.SCK
  N29: Mod1.GPIO8, Part6.CAN_CS
  N30: U1.+, M2.Pin_1, M3.Pin_1, Part1.VM, Part2.VM
  N31: Part1.B01, M4.pin_1
  N32: Part1.B02, M4.pin_2
  N33: Part1.A02, M5.pin_1
  N34: Part1.A01, M5.pin_2
  N35: Part2.B01, M6.pin_1
  N36: Part2.B02, M6.pin_2
  N37: Part2.A02, M7.pin_1
  N38: Part2.A01, M7.pin_2
  N39: Part6.CANH, Part7.CANH
  N40: Part6.CANL, Part7.CANL

notes:
  In practice, I use STM32F411CEU6 with 5 timer, STM32F401 will not have enough timer for 4 encoder+PWM. pin B11 on the schematic would be pin B2 on STM32F411
  Used WaveShare CAN HAT in practice
  Wire Color:
  Black: Ground
  Red:12V
  Orange:5V
  Yellow:3.3V
  White: Clock/PWM
  Grey: GPIO Output
  Purple/Light Brown: Input
  Dark Brown: Output
  Blue&Green: H-Bridge 12V Motor input
  Cyan&Pink: 5V CAN communication lines
  In practice, I used a MCP2515 module for SPI-CAN conversion
